# Fritzing sketch Fire_Car (saved by Fritzing 0.9.9b)
breadboards: 1

parts:
  Mod1 = Raspberry Pi 4B
  HC-SR04_Sensor_1 = HC-SR04 Ultrasonic Distance Sensor
  HC-SR04_Sensor_2 = HC-SR04 Ultrasonic Distance Sensor
  HC-SR04_Sensor_3 = HC-SR04 Ultrasonic Distance Sensor
  HC-SR04_Sensor_4 = HC-SR04 Ultrasonic Distance Sensor
  Part1 = Adafruit MLX90640 Thermal Camera [part_number="Adafruit #4407"]
  Mod2 = L298N DC motor driver
  M1 = DC Motor
  M2 = DC Motor

nets:
  3V3: Mod1.3V3, Part1.3.3V
  VCC: Mod1.5V, HC-SR04_Sensor_1.VCC, HC-SR04_Sensor_2.VCC, HC-SR04_Sensor_3.VCC, HC-SR04_Sensor_4.VCC
  N1: Mod1.GPIO2, Part1.SDA
  N2: Mod1.GPIO3, Part1.SCL
  GND: Mod1.GND, HC-SR04_Sensor_1.GND, HC-SR04_Sensor_2.GND, HC-SR04_Sensor_3.GND, HC-SR04_Sensor_4.GND, Part1.GND
  N3: Mod1.GPIO23, HC-SR04_Sensor_2.TRIG
  N4: Mod1.GPIO24, HC-SR04_Sensor_1.ECHO
  N5: Mod1.GPIO25, HC-SR04_Sensor_2.ECHO
  N6: Mod1.GPIO8, HC-SR04_Sensor_3.ECHO
  N7: Mod1.GPIO7, HC-SR04_Sensor_4.ECHO
  N8: Mod1.GPIO19, Mod2.IN3
  N9: Mod1.GPIO16, Mod2.IN1
  N10: Mod1.GPIO26, Mod2.IN4
  N11: Mod1.GPIO20, Mod2.IN2
  N12: HC-SR04_Sensor_1.TRIG, HC-SR04_Sensor_3.TRIG, HC-SR04_Sensor_4.TRIG
  N13: Mod2.OUT1, M1.pin_1
  N14: Mod2.OUT2, M1.pin_2
  N15: Mod2.OUT3, M2.pin_2
  N16: Mod2.OUT4, M2.pin_1

custom parts:
  Adafruit MLX90640 Thermal Camera: You can now add affordable heat-vision to your project and with an Adafruit MLX90640 Thermal Camera Breakout. This sensor contains a 24x32 array of IR thermal sensors. When connected to your microcontroller (or Raspberry Pi) it will return an array of 768 individual infrared temperature readings over I2C. It's like those fancy thermal cameras, but compact and simple enough for easy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
  L298N DC motor driver: 2x DC motor driver with 78M05 positive voltage regulator (7..35 V) L298N: max 46 V, 2 A Set 5 V Enable jumper to enable 5 V regultor (needed for the L298N) and +5 V output at screw terminal or supply external +5 V at screw terminal Set ENA and/or ENB to +5 V to enable motor permanently or supply ENA and/or ENB with PWM signal IN1 and IN2 set rotation directory for motor A (OUT1/OUT2) IN2 and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
